// Logisim project intro_to_digital_logic.circ as structural Verilog: 5 circuits, main circuit main
module main (
  input  a,
  input  b,
  input  c,
  output r
);

  wire and_1_out, or_1_out;

  and and_1 (and_1_out, b, c);
  or or_1 (or_1_out, a, and_1_out);
  not not_1 (r, or_1_out);
endmodule

module _1bit_adder_01_new (
  input  a,
  input  b,
  input  cin,
  output sum,
  output cout
);

  wire and_1_out, and_2_out, and_3_out, and_4_out, and_5_out, and_6_out, and_7_out, and_8_out;

  and and_1 (and_1_out, ~a, ~b, cin);  // AND_Gate
  and and_2 (and_2_out, ~a, b, ~cin);  // AND_Gate
  and and_3 (and_3_out, a, ~b, ~cin);  // AND_Gate
  and and_4 (and_4_out, a, b, cin);
  and and_5 (and_5_out, ~a, b, cin);  // AND_Gate
  and and_6 (and_6_out, a, ~b, cin);  // AND_Gate
  and and_7 (and_7_out, a, b, ~cin);  // AND_Gate
  and and_8 (and_8_out, a, b, cin);
  or or_1 (sum, and_1_out, and_2_out, and_3_out, and_4_out);
  or or_2 (cout, and_5_out, and_6_out, and_7_out, and_8_out);
endmodule

module _4bit_adder_new (
  input  cin,
  input  [3:0] a,
  input  [3:0] b,
  output [3:0] out_4,
  output cout
);

  wire n1bit_adder_01_new_1_cout, n1bit_adder_01_new_2_cout, n1bit_adder_01_new_3_cout;

  // Probe on a
  // Probe on b
  _1bit_adder_01_new u_1bit_adder_01_new_1 (
    .sum(out_4[0]), .cout(n1bit_adder_01_new_1_cout), .a(b[0]), .b(a[0]), .cin(cin));
  _1bit_adder_01_new u_1bit_adder_01_new_2 (
    .sum(out_4[1]), .cout(n1bit_adder_01_new_2_cout), .a(b[1]), .b(a[1]), .cin(n1bit_adder_01_new_1_cout));
  _1bit_adder_01_new u_1bit_adder_01_new_3 (
    .sum(out_4[2]), .cout(n1bit_adder_01_new_3_cout), .a(b[2]), .b(a[2]), .cin(n1bit_adder_01_new_2_cout));
  _1bit_adder_01_new u_1bit_adder_01_new_4 (
    .sum(out_4[3]), .cout(cout), .a(b[3]), .b(a[3]), .cin(n1bit_adder_01_new_3_cout));
  // Probe on out_4
endmodule

module counter (
  input  CLR,
  output [3:0] out_2
);

  wire clock_1_out;
  wire [3:0] adder_1_out;

  Clock clock_1 (.out(clock_1_out));
  Register #(.width(4)) register_1 (.D(adder_1_out), .en(1'b1), .Q(out_2), .clk(clock_1_out), .clr(CLR));
  Adder #(.width(4)) adder_1 (.a(out_2), .b(4'b0001), .out(adder_1_out), .cin(1'b0));  // open: cout
  // Probe on out_2
endmodule

module rom_led (
);

  wire [3:0] undriven;
  wire [7:0] rom_1_data;

  ROM #(.addrWidth(4)) rom_1 (.addr(undriven), .data(rom_1_data));  // open: sel

  // Notes on the sheet:
  //   contents of rom_1 (hex, n*v repeats v):
  //   ff 0 ff 0 ff 0 ff 0 ff ff 0 0 ff ff
endmodule
