// Logisim project data_memory_example.circ as structural Verilog: 2 circuits, main circuit main
module main (
  input  [31:0] in_1,
  input  [31:0] in_2,
  input  in_3,
  input  in_4,
  input  in_5,
  input  in_6,
  input  in_7,
  input  in_8,
  input  [3:0] in_9,
  output [31:0] out_10,
  output out_11
);

  wire [7:0] undriven;
  wire [15:0] bit_extender_1_out;

  RAM #(.dataWidth(32), .bus("separate")) ram_1 (
    .addr(in_1[9:2]), .din(in_2), .data(out_10), .str(in_4), .sel(in_5), .clk(in_3), .ld(in_6), .clr(in_7));
  assign bit_extender_1_out = {{8{1'b0}}, undriven};  // Bit_Extender bit_extender_1
  Decoder #(.select(4), .disabled(0)) decoder_1 (
    .out0(out_11), .sel(in_9), .en(in_8));  // open: out1, out2, out3, out4, out5, out6, out7, out8, out9, out10, out11, out12, out13, out14, out15
endmodule

module Conditional_Logic (
  input  CondEx,
  input  [1:0] FlagW,
  output FlagWrite0,
  output FlagWrite1
);

  and and_1 (FlagWrite0, CondEx, FlagW[0]);
  and and_2 (FlagWrite1, CondEx, FlagW[1]);
endmodule
